// Digital circuit FA.dig as structural Verilog
module FA (
  input  X,
  input  Y,
  input  Z,
  output S,
  output C
);

  wire and_1_out, and_2_out, xor_1_out;

  xor xor_1 (xor_1_out, X, Y);
  and and_1 (and_1_out, X, Y);
  xor xor_2 (S, xor_1_out, Z);
  and and_2 (and_2_out, Z, xor_1_out);
  or or_1 (C, and_2_out, and_1_out);
endmodule
