// Digital circuit adder_de_2bits.dig as structural Verilog
module adder_de_2bits (
  input  [1:0] A,
  input  [1:0] B,
  input  Cin,
  output [1:0] Sum,
  output Cout
);

  wire adder_1_cout;

  adder adder_1 (.A(A[0]), .B(B[0]), .Cin(Cin), .Sum(Sum[0]), .Cout(adder_1_cout));
  adder adder_2 (.A(A[1]), .B(B[1]), .Cin(adder_1_cout), .Sum(Sum[1]), .Cout(Cout));
endmodule
