// Digital circuit adder_de_4bits.dig as structural Verilog
module adder_de_4bits (
  input  [3:0] A,
  input  [3:0] B,
  input  Cin,
  output Cout,
  output [3:0] Sum
);

  wire adder_de_2bits_1_cout;

  adder_de_2bits adder_de_2bits_1 (.A(A[1:0]), .B(B[1:0]), .Cin(Cin), .Sum(Sum[1:0]), .Cout(adder_de_2bits_1_cout));
  adder_de_2bits adder_de_2bits_2 (.A(A[3:2]), .B(B[3:2]), .Cin(adder_de_2bits_1_cout), .Sum(Sum[3:2]), .Cout(Cout));
endmodule
