// Digital circuit adder_de_8bits.dig as structural Verilog
module adder_de_8bits (
  input  [7:0] A,
  input  Cin,
  input  [7:0] B,
  output [7:0] S,
  output Cout
);

  wire adder_de_4bits_1_cout;

  adder_de_4bits adder_de_4bits_1 (.A(A[3:0]), .B(B[3:0]), .Cin(Cin), .Cout(adder_de_4bits_1_cout), .Sum(S[3:0]));
  adder_de_4bits adder_de_4bits_2 (.A(A[7:4]), .B(B[7:4]), .Cin(adder_de_4bits_1_cout), .Cout(Cout), .Sum(S[7:4]));
endmodule
