// Digital circuit alu.dig as structural Verilog
module alu (
  input  [7:0] A,
  input  [7:0] B,
  input  [3:0] Op,
  output [7:0] S
);

  wire [7:0] Sadd, Sdec, Sdiv, Sinc, Slsh, Smul, Srsh, Ssub;

  adder_de_8bits adder_de_8bits_1 (.A(A), .Cin(1'b0), .B(B), .S(Sadd));  // open: Cout
  // Divider_8bits divider_8bits_1: pin names not known; wires that end beside it: A[3:0], B[3:0], Sdiv[3:0], Sdiv[7:4]
  shifter_right shifter_right_1 (.In(A), .Out(Srsh));  // open: Cout
  subtrator_de_8bits subtrator_de_8bits_1 (.A(A), .B(B), .S(Ssub));  // open: Cout
  incremento_de_8bits incremento_de_8bits_1 (.In(A), .Out(Sinc));
  shifter shifter_1 (.In(A), .Out(Slsh));  // open: Cout
  multiplicador_de_4bits multiplicador_de_4bits_1 (.A(A[3:0]), .B(B[3:0]), .P(Smul));
  decremento_de_8bits decremento_de_8bits_1 (.In(A), .Out(Sdec));
  Multiplexer #(.Selector_Bits(4), .Bits(8)) multiplexer_1 (
    .sel(Op), .in_0(Sadd), .in_1(Ssub), .in_2(Sinc), .in_3(Sdec), .in_4(Srsh), .in_5(Slsh), .in_6(Smul),
    .in_7(Sdiv), .in_8({8{1'b0}}), .in_9({8{1'b0}}), .in_10({8{1'b0}}), .in_11({8{1'b0}}), .in_12({8{1'b0}}),
    .in_13({8{1'b0}}), .in_14({8{1'b0}}), .in_15({8{1'b0}}), .out(S));
endmodule
