// Digital circuit cpu.dig as structural Verilog
module cpu (
  input  CLK,
  input  CLR,
  output Cout,
  output Out0,
  output Out1,
  output Out2,
  output Out3,
  output Out4,
  output Out5,
  output Out6,
  output Out7
);

  wire Clock, Controller_p1, Cp, Ea, Ep, Eu, nCe, nEl, nL0, nLa, nLb, nLi, nLm, not_1_out, not_2_out,
       not_3_out, not_4_out, not_5_out, not_6_out, not_7_out, not_8_out, Su, x0, x1, x2, x3, x4, x5, x6, x7;
  wire [3:0] IR_y0, IR_y5, MAR_y0;
  wire [7:0] A_y0, B_y0, bitextender_1_out, driver_5_out, ula_1_p1, ula_1_p4;

  not not_1 (not_1_out, nLm);
  pc pc_1 (.Count(Cp), .Clr(CLR), .Clk(Clock), .Enable(Ep), .C3(x3), .C2(x2), .C1(x1), .C0(x0));
  not not_2 (not_2_out, nCe);
  not not_3 (not_3_out, Controller_p1);
  register_4bits MAR (
    .X3(x3), .X2(x2), .X1(x1), .X0(x0), .Load(not_1_out), .Clk(Clock), .Clr(CLR), .Enable(1'b1),
    .Y3(MAR_y0[3]), .Y2(MAR_y0[2]), .Y1(MAR_y0[1]), .Y0(MAR_y0[0]));
  ROM #(.AddrBits(4), .Bits(8)) rom_1 (.A(MAR_y0), .sel(not_2_out), .D({x7, x6, x5, x4, x3, x2, x1, x0}));
  not not_4 (not_4_out, nLi);
  register_8bits IR (
    .X3(x3), .X2(x2), .X1(x1), .X0(x0), .Load(not_4_out), .Clk(Clock), .Clr(CLR), .Enable(1'b1), .X4(x4),
    .X5(x5), .X6(x6), .X7(x7), .Y3(IR_y0[3]), .Y2(IR_y0[2]), .Y1(IR_y0[1]), .Y0(IR_y0[0]), .Y4(IR_y5[0]),
    .Y5(IR_y5[1]), .Y6(IR_y5[2]), .Y7(IR_y5[3]));
  // controller Controller: pin names not known; wires that end beside it: Controller_p1, nL0, nLb, Eu, Su, Ea, nLa, nEl, nCe, nLm, IR_y5, nLi, CLR, Cp, Clock, Ep, {x7, x6, x5, x4}, {x3, x2, x1, x0}
  assign Clock = not_3_out ? CLK : 1'bz;  // Driver driver_1
  assign {x3, x2, x1, x0} = not_5_out ? IR_y0 : 4'bz;  // Driver driver_2
  not not_5 (not_5_out, nEl);
  register_8bits A (
    .X3(x3), .X2(x2), .X1(x1), .X0(x0), .Load(not_6_out), .Clk(Clock), .Clr(CLR), .Enable(1'b1), .X4(x4),
    .X5(x5), .X6(x6), .X7(x7), .Y3(A_y0[3]), .Y2(A_y0[2]), .Y1(A_y0[1]), .Y0(A_y0[0]), .Y4(A_y0[4]),
    .Y5(A_y0[5]), .Y6(A_y0[6]), .Y7(A_y0[7]));
  not not_6 (not_6_out, nLa);
  assign {x7, x6, x5, x4, x3, x2, x1, x0} = Ea ? A_y0 : 8'bz;  // Driver driver_3
  assign {x7, x6, x5, x4, x3, x2, x1, x0} = Eu ? ula_1_p1 : 8'bz;  // Driver driver_4
  not not_7 (not_7_out, nLb);
  not not_8 (not_8_out, nL0);
  register_8bits B (
    .X3(x3), .X2(x2), .X1(x1), .X0(x0), .Load(not_7_out), .Clk(Clock), .Clr(CLR), .Enable(1'b1), .X4(x4),
    .X5(x5), .X6(x6), .X7(x7), .Y3(B_y0[3]), .Y2(B_y0[2]), .Y1(B_y0[1]), .Y0(B_y0[0]), .Y4(B_y0[4]),
    .Y5(B_y0[5]), .Y6(B_y0[6]), .Y7(B_y0[7]));
  register_8bits Out (
    .X3(x3), .X2(x2), .X1(x1), .X0(x0), .Load(not_8_out), .Clk(Clock), .Clr(CLR), .Enable(1'b1), .X4(x4),
    .X5(x5), .X6(x6), .X7(x7), .Y3(Out3), .Y2(Out2), .Y1(Out1), .Y0(Out0), .Y4(Out4), .Y5(Out5), .Y6(Out6),
    .Y7(Out7));
  // ula ula_1: pin names not known; wires that end beside it: ula_1_p1, Cout, Su, ula_1_p4, A_y0
  assign ula_1_p4 = B_y0 ^ driver_5_out;  // XOr xor_1, 8 bits wide
  BitExtender #(.inputBits(1), .outputBits(8)) bitextender_1 (.in(Su), .out(bitextender_1_out));
  assign driver_5_out = Su ? bitextender_1_out : 8'bz;  // Driver driver_5
  Seven_Seg_Hex seven_seg_hex_1 (.d({Out7, Out6, Out5, Out4}), .dp(1'b0));
  Seven_Seg_Hex seven_seg_hex_2 (.d({Out3, Out2, Out1, Out0}), .dp(1'b0));

  // Other names for the same wires on the sheet: Clear = CLR

  // Notes on the sheet:
  //   contents of rom_1 (hex, n*v repeats v):
  //   8,19,2a,e0,f0,0,0,0,5,3
  //   HIGH
  //   LOW
endmodule
