// Digital circuit decremento_de_8bits.dig as structural Verilog
module decremento_de_8bits (
  input  [7:0] In,
  output [7:0] Out
);

  adder_de_8bits adder_de_8bits_1 (.A(In), .Cin(1'b0), .B({8{1'b1}}), .S(Out));  // open: Cout
endmodule
