// Digital circuit incremento_de_8bits.dig as structural Verilog
module incremento_de_8bits (
  input  [7:0] In,
  output [7:0] Out
);

  adder_de_8bits adder_de_8bits_1 (.A(In), .Cin(1'b0), .B(8'h1), .S(Out));  // open: Cout
endmodule
