// Digital circuit instruction_decoder.dig as structural Verilog
module instruction_decoder (
  input  I7,
  input  I6,
  input  I5,
  input  I4,
  output Lda,
  output Add,
  output Sub,
  output Out,
  output Hlt
);

  wire not_1_out, not_2_out, not_3_out, not_4_out;

  not not_1 (not_1_out, I7);
  not not_2 (not_2_out, I6);
  not not_3 (not_3_out, I5);
  not not_4 (not_4_out, I4);
  and and_1 (Lda, not_1_out, not_2_out, not_3_out, not_4_out);
  and and_2 (Add, not_1_out, not_2_out, not_3_out, I4);
  and and_3 (Sub, not_1_out, not_2_out, I5, not_4_out);
  and and_4 (Out, I7, I6, I5, not_4_out);
  and and_5 (Hlt, I7, I6, I5, I4);
endmodule
