// Digital circuit multiplicador_de_2bits.dig as structural Verilog
module multiplicador_de_2bits (
  input  [1:0] A,
  input  [1:0] B,
  output [3:0] R
);

  wire [1:0] multiplicador_parcial_1_r, multiplicador_parcial_2_r;
  wire [3:0] shifter_de_4bits_1_r;

  multiplicador_parcial multiplicador_parcial_1 (.A(A[0]), .B(B), .R(multiplicador_parcial_1_r));
  multiplicador_parcial multiplicador_parcial_2 (.A(A[1]), .B(B), .R(multiplicador_parcial_2_r));
  shifter_de_4bits shifter_de_4bits_1 (
    .A({2'b00, multiplicador_parcial_2_r}), .Cin(1'b0), .R(shifter_de_4bits_1_r));  // open: Cout
  adder_de_4bits adder_de_4bits_1 (
    .A(shifter_de_4bits_1_r), .B({2'b00, multiplicador_parcial_1_r}), .Cin(1'b0), .Sum(R));  // open: Cout
endmodule
