// Digital circuit multiplicador_de_4bits.dig as structural Verilog
module multiplicador_de_4bits (
  input  [3:0] A,
  input  [3:0] B,
  output [7:0] P
);

  wire adder_de_8bits_1_cout, adder_de_8bits_2_cout;
  wire [3:0] multiplicador_de_2bits_1_r, multiplicador_de_2bits_2_r, multiplicador_de_2bits_3_r,
       multiplicador_de_2bits_4_r;
  wire [7:0] adder_de_8bits_1_s, adder_de_8bits_2_s, shifter_1_out, shifter_2_out, shifter_3_out,
       shifter_4_out, shifter_5_out, shifter_6_out, shifter_7_out, shifter_8_out;

  multiplicador_de_2bits multiplicador_de_2bits_1 (.A(A[1:0]), .B(B[1:0]), .R(multiplicador_de_2bits_1_r));
  multiplicador_de_2bits multiplicador_de_2bits_2 (.A(A[1:0]), .B(B[3:2]), .R(multiplicador_de_2bits_2_r));
  multiplicador_de_2bits multiplicador_de_2bits_3 (.A(A[3:2]), .B(B[1:0]), .R(multiplicador_de_2bits_3_r));
  multiplicador_de_2bits multiplicador_de_2bits_4 (.A(A[3:2]), .B(B[3:2]), .R(multiplicador_de_2bits_4_r));
  shifter shifter_1 (.In({4'b0000, multiplicador_de_2bits_2_r}), .Out(shifter_1_out));  // open: Cout
  shifter shifter_2 (.In({4'b0000, multiplicador_de_2bits_3_r}), .Out(shifter_2_out));  // open: Cout
  shifter shifter_3 (.In({4'b0000, multiplicador_de_2bits_4_r}), .Out(shifter_3_out));  // open: Cout
  shifter shifter_4 (.In(shifter_1_out), .Out(shifter_4_out));  // open: Cout
  shifter shifter_5 (.In(shifter_2_out), .Out(shifter_5_out));  // open: Cout
  shifter shifter_6 (.In(shifter_3_out), .Out(shifter_6_out));  // open: Cout
  shifter shifter_7 (.In(shifter_6_out), .Out(shifter_7_out));  // open: Cout
  adder_de_8bits adder_de_8bits_1 (
    .A({4'b0000, multiplicador_de_2bits_1_r}), .Cin(1'b0), .B(shifter_4_out), .S(adder_de_8bits_1_s),
    .Cout(adder_de_8bits_1_cout));
  shifter shifter_8 (.In(shifter_7_out), .Out(shifter_8_out));  // open: Cout
  adder_de_8bits adder_de_8bits_2 (
    .A(adder_de_8bits_1_s), .Cin(adder_de_8bits_1_cout), .B(shifter_5_out), .S(adder_de_8bits_2_s),
    .Cout(adder_de_8bits_2_cout));
  adder_de_8bits adder_de_8bits_3 (
    .A(adder_de_8bits_2_s), .Cin(adder_de_8bits_2_cout), .B(shifter_8_out), .S(P));  // open: Cout
endmodule
