// Digital circuit multiplicador_parcial.dig as structural Verilog
module multiplicador_parcial (
  input  A,
  input  [1:0] B,
  output [1:0] R
);

  and and_1 (R[1], A, B[1]);
  and and_2 (R[0], A, B[0]);
endmodule
