// Digital circuit pc.dig as structural Verilog
module pc (
  input  Count,
  input  Clr,
  input  Clk,
  input  Enable,
  output C3,
  output C2,
  output C1,
  output C0
);

  wire and_1_out, and_2_out, and_3_out, jk_ff_as_1_q, jk_ff_as_2_q, jk_ff_as_3_q, jk_ff_as_4_q;

  and and_1 (and_1_out, jk_ff_as_2_q, and_2_out, Count);
  JK_FF_AS jk_ff_as_1 (.Set(1'b0), .J(and_1_out), .C(Clk), .K(and_1_out), .Clr(Clr), .Q(jk_ff_as_1_q));  // open: nQ
  assign C3 = Enable ? jk_ff_as_1_q : 1'bz;  // Driver driver_1
  and and_2 (and_2_out, jk_ff_as_3_q, and_3_out, Count);
  JK_FF_AS jk_ff_as_2 (.Set(1'b0), .J(and_2_out), .C(Clk), .K(and_2_out), .Clr(Clr), .Q(jk_ff_as_2_q));  // open: nQ
  assign C2 = Enable ? jk_ff_as_2_q : 1'bz;  // Driver driver_2
  and and_3 (and_3_out, jk_ff_as_4_q, Count);
  JK_FF_AS jk_ff_as_3 (.Set(1'b0), .J(and_3_out), .C(Clk), .K(and_3_out), .Clr(Clr), .Q(jk_ff_as_3_q));  // open: nQ
  assign C1 = Enable ? jk_ff_as_3_q : 1'bz;  // Driver driver_3
  JK_FF_AS jk_ff_as_4 (.Set(1'b0), .J(Count), .C(Clk), .K(Count), .Clr(Clr), .Q(jk_ff_as_4_q));  // open: nQ
  assign C0 = Enable ? jk_ff_as_4_q : 1'bz;  // Driver driver_4
endmodule
