// Digital circuit rc.dig as structural Verilog
module rc (
  input  Clk,
  input  Clr,
  output T6,
  output T5,
  output T4,
  output T3,
  output T2,
  output T1
);

  wire jk_ff_as_1_nq, jk_ff_as_2_nq, jk_ff_as_3_nq, jk_ff_as_4_nq, jk_ff_as_5_nq, jk_ff_as_6_q;

  JK_FF_AS jk_ff_as_1 (.Set(1'b0), .J(T5), .C(Clk), .K(jk_ff_as_2_nq), .Clr(Clr), .Q(T6), .nQ(jk_ff_as_1_nq));
  JK_FF_AS jk_ff_as_2 (.Set(1'b0), .J(T4), .C(Clk), .K(jk_ff_as_3_nq), .Clr(Clr), .Q(T5), .nQ(jk_ff_as_2_nq));
  JK_FF_AS jk_ff_as_3 (.Set(1'b0), .J(T3), .C(Clk), .K(jk_ff_as_4_nq), .Clr(Clr), .Q(T4), .nQ(jk_ff_as_3_nq));
  JK_FF_AS jk_ff_as_4 (.Set(1'b0), .J(T2), .C(Clk), .K(jk_ff_as_5_nq), .Clr(Clr), .Q(T3), .nQ(jk_ff_as_4_nq));
  JK_FF_AS jk_ff_as_5 (.Set(1'b0), .J(T1), .C(Clk), .K(jk_ff_as_6_q), .Clr(Clr), .Q(T2), .nQ(jk_ff_as_5_nq));
  JK_FF_AS jk_ff_as_6 (.Set(1'b0), .J(jk_ff_as_1_nq), .C(Clk), .K(T6), .Clr(Clr), .Q(jk_ff_as_6_q), .nQ(T1));
endmodule
