// Digital circuit register_4bits.dig as structural Verilog
module register_4bits (
  input  X3,
  input  X2,
  input  X1,
  input  X0,
  input  Load,
  input  Clk,
  input  Clr,
  input  Enable,
  output Y3,
  output Y2,
  output Y1,
  output Y0
);

  wire and_1_out, and_2_out, and_3_out, and_4_out, and_5_out, and_6_out, and_7_out, and_8_out, d_ff_as_1_q,
       d_ff_as_2_q, d_ff_as_3_q, d_ff_as_4_q, not_1_out, or_1_out, or_2_out, or_3_out, or_4_out;

  and and_1 (and_1_out, not_1_out, d_ff_as_1_q);
  D_FF_AS d_ff_as_1 (.Set(1'b0), .D(or_1_out), .C(Clk), .Clr(Clr), .Q(d_ff_as_1_q));  // open: nQ
  and and_2 (and_2_out, Load, X3);
  or or_1 (or_1_out, and_2_out, and_1_out);
  assign Y3 = Enable ? d_ff_as_1_q : 1'bz;  // Driver driver_1
  and and_3 (and_3_out, not_1_out, d_ff_as_2_q);
  D_FF_AS d_ff_as_2 (.Set(1'b0), .D(or_2_out), .C(Clk), .Clr(Clr), .Q(d_ff_as_2_q));  // open: nQ
  and and_4 (and_4_out, Load, X2);
  or or_2 (or_2_out, and_4_out, and_3_out);
  assign Y2 = Enable ? d_ff_as_2_q : 1'bz;  // Driver driver_2
  and and_5 (and_5_out, not_1_out, d_ff_as_3_q);
  or or_3 (or_3_out, and_6_out, and_5_out);
  D_FF_AS d_ff_as_3 (.Set(1'b0), .D(or_3_out), .C(Clk), .Clr(Clr), .Q(d_ff_as_3_q));  // open: nQ
  and and_6 (and_6_out, Load, X1);
  assign Y1 = Enable ? d_ff_as_3_q : 1'bz;  // Driver driver_3
  and and_7 (and_7_out, not_1_out, d_ff_as_4_q);
  or or_4 (or_4_out, and_8_out, and_7_out);
  D_FF_AS d_ff_as_4 (.Set(1'b0), .D(or_4_out), .C(Clk), .Clr(Clr), .Q(d_ff_as_4_q));  // open: nQ
  and and_8 (and_8_out, Load, X0);
  assign Y0 = Enable ? d_ff_as_4_q : 1'bz;  // Driver driver_4
  not not_1 (not_1_out, Load);
endmodule
