// Digital circuit register_8bits.dig as structural Verilog
module register_8bits (
  input  X3,
  input  X2,
  input  X1,
  input  X0,
  input  Load,
  input  Clk,
  input  Clr,
  input  Enable,
  input  X4,
  input  X5,
  input  X6,
  input  X7,
  output Y3,
  output Y2,
  output Y1,
  output Y0,
  output Y4,
  output Y5,
  output Y6,
  output Y7
);

  wire and_1_out, and_2_out, and_3_out, and_4_out, and_5_out, and_6_out, and_7_out, and_8_out, and_9_out,
       and_10_out, and_11_out, and_12_out, and_13_out, and_14_out, and_15_out, and_16_out, d_ff_as_1_q,
       d_ff_as_2_q, d_ff_as_3_q, d_ff_as_4_q, d_ff_as_5_q, d_ff_as_6_q, d_ff_as_7_q, d_ff_as_8_q, not_1_out,
       or_1_out, or_2_out, or_3_out, or_4_out, or_5_out, or_6_out, or_7_out, or_8_out;

  and and_1 (and_1_out, not_1_out, d_ff_as_1_q);
  or or_1 (or_1_out, and_2_out, and_1_out);
  D_FF_AS d_ff_as_1 (.Set(1'b0), .D(or_1_out), .C(Clk), .Clr(Clr), .Q(d_ff_as_1_q));  // open: nQ
  and and_2 (and_2_out, Load, X7);
  assign Y7 = Enable ? d_ff_as_1_q : 1'bz;  // Driver driver_1
  and and_3 (and_3_out, not_1_out, d_ff_as_2_q);
  D_FF_AS d_ff_as_2 (.Set(1'b0), .D(or_2_out), .C(Clk), .Clr(Clr), .Q(d_ff_as_2_q));  // open: nQ
  or or_2 (or_2_out, and_4_out, and_3_out);
  assign Y6 = Enable ? d_ff_as_2_q : 1'bz;  // Driver driver_2
  and and_4 (and_4_out, Load, X6);
  and and_5 (and_5_out, not_1_out, d_ff_as_3_q);
  D_FF_AS d_ff_as_3 (.Set(1'b0), .D(or_3_out), .C(Clk), .Clr(Clr), .Q(d_ff_as_3_q));  // open: nQ
  and and_6 (and_6_out, Load, X5);
  or or_3 (or_3_out, and_6_out, and_5_out);
  assign Y5 = Enable ? d_ff_as_3_q : 1'bz;  // Driver driver_3
  and and_7 (and_7_out, not_1_out, d_ff_as_4_q);
  or or_4 (or_4_out, and_8_out, and_7_out);
  D_FF_AS d_ff_as_4 (.Set(1'b0), .D(or_4_out), .C(Clk), .Clr(Clr), .Q(d_ff_as_4_q));  // open: nQ
  and and_8 (and_8_out, Load, X4);
  assign Y4 = Enable ? d_ff_as_4_q : 1'bz;  // Driver driver_4
  and and_9 (and_9_out, not_1_out, d_ff_as_5_q);
  D_FF_AS d_ff_as_5 (.Set(1'b0), .D(or_5_out), .C(Clk), .Clr(Clr), .Q(d_ff_as_5_q));  // open: nQ
  and and_10 (and_10_out, Load, X3);
  or or_5 (or_5_out, and_10_out, and_9_out);
  assign Y3 = Enable ? d_ff_as_5_q : 1'bz;  // Driver driver_5
  and and_11 (and_11_out, not_1_out, d_ff_as_6_q);
  D_FF_AS d_ff_as_6 (.Set(1'b0), .D(or_6_out), .C(Clk), .Clr(Clr), .Q(d_ff_as_6_q));  // open: nQ
  and and_12 (and_12_out, Load, X2);
  or or_6 (or_6_out, and_12_out, and_11_out);
  assign Y2 = Enable ? d_ff_as_6_q : 1'bz;  // Driver driver_6
  and and_13 (and_13_out, not_1_out, d_ff_as_7_q);
  or or_7 (or_7_out, and_14_out, and_13_out);
  D_FF_AS d_ff_as_7 (.Set(1'b0), .D(or_7_out), .C(Clk), .Clr(Clr), .Q(d_ff_as_7_q));  // open: nQ
  and and_14 (and_14_out, Load, X1);
  assign Y1 = Enable ? d_ff_as_7_q : 1'bz;  // Driver driver_7
  and and_15 (and_15_out, not_1_out, d_ff_as_8_q);
  or or_8 (or_8_out, and_16_out, and_15_out);
  D_FF_AS d_ff_as_8 (.Set(1'b0), .D(or_8_out), .C(Clk), .Clr(Clr), .Q(d_ff_as_8_q));  // open: nQ
  and and_16 (and_16_out, Load, X0);
  assign Y0 = Enable ? d_ff_as_8_q : 1'bz;  // Driver driver_8
  not not_1 (not_1_out, Load);
endmodule
