// Digital circuit shifter_de_4bits.dig as structural Verilog
module shifter_de_4bits (
  input  [3:0] A,
  input  Cin,
  output Cout,
  output [3:0] R
);


  assign Cout = A[3];
  assign R = {A[2:0], Cin};
endmodule
