// Digital circuit shifter_right.dig as structural Verilog
module shifter_right (
  input  [7:0] In,
  output [7:0] Out,
  output Cout
);


  assign Cout = In[0];
  assign Out = {1'b0, In[7:1]};
endmodule
