// Digital circuit subtrator_de_8bits.dig as structural Verilog
module subtrator_de_8bits (
  input  [7:0] A,
  input  [7:0] B,
  output [7:0] S,
  output Cout
);

  wire [7:0] not_1_out;

  assign not_1_out = ~B;  // Not not_1, 8 bits wide
  adder_de_8bits adder_de_8bits_1 (.A(A), .Cin(1'b1), .B(not_1_out), .S(S), .Cout(Cout));
endmodule
